# Fritzing sketch handheldspedo (saved by Fritzing 0.9.3b)
circuit board: 6.29169cm x 5.9667cm
breadboards: 1

parts:
  Raspberry_Pi_1 = Raspberry Pi 3 [part_number=RPI-3-V1.2]
  Part1 = Triple Axis Accelerometer Breakout - ADXL345

nets:
  3V3: Raspberry_Pi_1.3v3, Part1.VCC
  N1: Raspberry_Pi_1.GPIO2, Part1.SDA
  N2: Raspberry_Pi_1.GPIO3, Part1.SCL
  GND: Raspberry_Pi_1.GND, Part1.GND

notes:
  Dariusz Kulpinski
  CENG 317
  Breadboard Wiring Diagram
  RED [VCC - 3.3V (Pin 1)]
  BLACK [GND - GND (Pin 38)]
  BLUE [SDA - SDA1 I2C (Pin 2)]
  YELLOW [SCL - SCL1 I2C (Pin 3)]
  Dariusz Kulpinski
  CENG317 Project
  Handheld Spedometer
  PCB Top
  PCB Bottom
  <- Raspberry Pi 3 V+ GPIO
  ADXL345 Accelerometer
  GND
  VCC (3.3V)
  SCL
  SDA
  Dariusz Kulpinski
  CENG 317 - 0NB
  HandHeld Spedometer
  Wiring Schematic
  November 06th, 2018
  Red - VCC 3.3v
  Blue - I2C SDA Data Bus
  Yellow - I2C SCL Clock Bus
  Black - GND Ground

// code stored in the sketch: Untitled2.ino
no code here LMAO
